# Fritzing sketch auto bluetooth (saved by Fritzing 1.0.3b)
breadboards: 1

parts:
  S1 = H-Bridge with L298N
  M1 = gear-motor
  M2 = gear-motor
  M3 = gear-motor
  M4 = gear-motor
  Componente1 = Arduino Uno (Rev3)
  Componente2 = Bluetooth HC-05 Macho
  VCC1 = Battery block 9V [internal_resistance=0.1Ω]

nets:
  N1: S1.12V, VCC1.+
  GND: S1.GND, Componente1.GND, Componente2.GND, VCC1.-
  5V: S1.5V, Componente1.5V, Componente2.VCC
  N2: S1.IN1, Componente1.D12/MISO
  N3: S1.IN2, Componente1.D11_PWM/MOSI
  N4: S1.IN3, Componente1.D10_PWM/SS
  N5: S1.IN4, Componente1.D9_PWM
  N6: S1.M1-01, M3.pin_2, M4.pin_2
  N7: S1.M1-02, M3.pin_1, M4.pin_1
  N8: S1.M2-01, M1.pin_2, M2.pin_2
  N9: S1.M2-02, M1.pin_1, M2.pin_1
  N10: Componente1.D0/RX, Componente2.TXD
  N11: Componente1.D1/TX, Componente2.RXD

custom parts:
  H-Bridge with L298N: h-bridge

// code stored in the sketch: auto blue.ino
char t;
 
void setup() {
pinMode(13,OUTPUT);   //motor izquierdo delantero
pinMode(12,OUTPUT);   //motor izquierdo trasero
pinMode(11,OUTPUT);   //motor derecho delantero
pinMode(10,OUTPUT);   //motor derecho trasero
Serial.begin(9600);
}
 
void loop() {
if(Serial.available()){
  t = Serial.read();
  Serial.println(t);
}
 
if(t == 'F'){            //mover hacia adelante
  digitalWrite(13,HIGH);
  digitalWrite(11,HIGH);
}
 
else if(t == 'B'){      //mover hacia atras
  digitalWrite(12,HIGH);
  digitalWrite(10,HIGH);
}
 
else if(t == 'L'){      //girar a la derecha 
  digitalWrite(11,HIGH);
}
 
else if(t == 'R'){      //girar a la izquierda 
  digitalWrite(13,HIGH);
}
 
else if(t == 'S'){      //STOP 
  digitalWrite(13,LOW);
  digitalWrite(12,LOW);
  digitalWrite(11,LOW);
  digitalWrite(10,LOW);
}
delay(100);
}
